# Fritzing sketch PiUnit (saved by Fritzing 0.9.10b)
breadboards: 1

parts:
  DC/DC_5V_3A_Conv = RioRand LM2596
  DC/DC_5V_3A_conv = RioRand LM2596
  MCU1 = Raspberry Pi Zero
  IC1 = ULN2803A [package=THT]
  AC_control_Header = Header 10 [package=1x10-2mm-smd]
  R1 = Resistor [tolerance=±5% power=0.25 resistance=4.7k package=THT]
  R2 = Resistor [tolerance=±5% power=0.25 resistance=4.7k package=THT]
  R3 = Resistor [tolerance=±5% power=0.25 resistance=4.7k package=THT]
  R4 = Resistor [tolerance=±5% power=0.25 resistance=4.7k package=THT]
  R5 = Resistor [tolerance=±5% power=0.25 resistance=4.7k package=THT]
  R6 = Resistor [tolerance=±5% power=0.25 resistance=4.7k package=THT]
  R7 = Resistor [tolerance=±5% power=0.25 resistance=4.7k package=THT]
  R8 = Resistor [tolerance=±5% power=0.25 resistance=4.7k package=THT]
  PWM_OUT_1 = Header 2 [package=jst-2-pth-kit]
  PWM_OUT_2 = Header 2 [package=jst-2-pth-kit]
  DS18B20_OUT1 = Header 3 [package=jst-3-smd]
  GPIO_OUT_2_(Level_shifted) = Header 3 [package=jst-3-smd]
  GPIO_OUT_3_(Level_shifted) = Header 3 [package=jst-3-smd]
  GPIO_OUT_4_(Level_shifted) = Header 3 [package=jst-3-smd]
  GPIO_? = Header 1 [package=1x01_offset]
  GPIO1 = Header 1 [package=1x01_offset]
  GPIO2 = Header 1 [package=1x01_offset]
  GPIO3 = Header 1 [package=1x01_offset]
  GPIO = Header 1 [package=1x01_offset]
  GPIO_?1 = Header 1 [package=1x01_offset]
  GPIO_?2 = Header 1 [package=1x01_offset]
  GPIO_?3 = Header 1 [package=1x01_offset]
  12V_+_5V_MOLEX_Adapter = screw terminal, 4 pins
  U1 = mystery part, 12 pins [chip_label=BSS138]
  USB_socket = USB connector [package=THT]
  U2 = mystery part, 4 pins [chip_label="I2C Boost" part_number=LTC4311]
  U3 = mystery part, 8 pins [chip_label="I2C Isolator" part_number=LTC1540]
  DS18B20_OUT2 = Header 3 [package=jst-3-smd]
  Doser_GPIO_Out_(DB9) = female pin header, 9 pins [form="♀ (female)"]
  limit_resistors = Resistor [tolerance=±5% power=0.25 resistance=1.3k package=THT]
  R10 = Resistor [tolerance=±5% power=0.25 resistance=1.3k package=THT]
  R11 = Resistor [tolerance=±5% power=0.25 resistance=1.3k package=THT]
  R12 = Resistor [tolerance=±5% power=0.25 resistance=1.3k package=THT]

nets:
  N1: DC/DC_5V_3A_Conv.Pin_1, DC/DC_5V_3A_conv.Pin_1, 12V_+_5V_MOLEX_Adapter.pin1
  N2: DC/DC_5V_3A_Conv.Pin_2, DC/DC_5V_3A_conv.Pin_2, 12V_+_5V_MOLEX_Adapter.pin2
  N3: DC/DC_5V_3A_Conv.Pin_3, MCU1.pin_2, IC1.COM_-_Common, AC_control_Header.1, R1.Pin_1, R2.Pin_1, R3.Pin_1, R4.Pin_1, R5.Pin_1, R6.Pin_1, R7.Pin_1, R8.Pin_1, DS18B20_OUT1.1, GPIO_OUT_2_(Level_shifted).1, GPIO_OUT_3_(Level_shifted).1, GPIO_OUT_4_(Level_shifted).1, U1.pin7, USB_socket.5V, U2.pin1, U3.pin1, DS18B20_OUT2.1
  N4: DC/DC_5V_3A_Conv.Pin_4, MCU1.pin_6, MCU1.pin_9, MCU1.pin_30, MCU1.pin_39, IC1.0V, AC_control_Header.10, PWM_OUT_1.2, PWM_OUT_2.2, U1.pin6, USB_socket.chassis6, U2.pin4, U3.pin4, U3.pin8
  N5: DC/DC_5V_3A_conv.Pin_3, 12V_+_5V_MOLEX_Adapter.pin4
  N6: DC/DC_5V_3A_conv.Pin_4, 12V_+_5V_MOLEX_Adapter.pin3
  N7: MCU1.pin_1, MCU1.pin_17, U1.pin5, U3.pin5
  N8: MCU1.pin_3, U3.pin6
  N9: MCU1.pin_5, U3.pin7
  N10: MCU1.pin_7, U1.pin1
  N11: MCU1.pin_8, U1.pin3
  N12: MCU1.pin_10, U1.pin4
  N13: MCU1.pin_11, U1.pin2
  N14: MCU1.pin_12, PWM_OUT_1.1
  N15: MCU1.pin_13, IC1.In_8
  N16: MCU1.pin_15, IC1.In_7
  N17: MCU1.pin_16, IC1.In_1
  N18: MCU1.pin_18, IC1.In_2
  N19: MCU1.pin_19, GPIO_?.1
  N20: MCU1.pin_21, GPIO1.1
  N21: MCU1.pin_22, IC1.In_3
  N22: MCU1.pin_23, GPIO2.1
  N23: MCU1.pin_24, GPIO_?1.1
  N24: MCU1.pin_26, GPIO_?2.1
  N25: MCU1.pin_27, GPIO3.1
  N26: MCU1.pin_28, GPIO_?3.1
  N27: MCU1.pin_29, IC1.In_4
  N28: MCU1.pin_31, IC1.In_5
  N29: MCU1.pin_32, IC1.In_6
  N30: MCU1.pin_33, limit_resistors.Pin_0
  N31: MCU1.pin_35, PWM_OUT_2.1
  N32: MCU1.pin_36, R10.Pin_0
  N33: MCU1.pin_37, GPIO.1
  N34: MCU1.pin_38, R11.Pin_0
  N35: MCU1.pin_40, R12.Pin_0
  N36: IC1.Out_8, AC_control_Header.9, R8.Pin_0
  N37: IC1.Out_7, AC_control_Header.8, R7.Pin_0
  N38: IC1.Out_6, AC_control_Header.7, R6.Pin_0
  N39: IC1.Out_5, AC_control_Header.6, R5.Pin_0
  N40: IC1.Out_4, AC_control_Header.5, R4.Pin_0
  N41: IC1.Out_3, AC_control_Header.4, R3.Pin_0
  N42: IC1.Out_2, AC_control_Header.3, R2.Pin_0
  N43: IC1.Out_1, AC_control_Header.2, R1.Pin_0
  N44: DS18B20_OUT1.2, U1.pin9, DS18B20_OUT2.2
  N45: DS18B20_OUT1.3, GPIO_OUT_2_(Level_shifted).3, GPIO_OUT_3_(Level_shifted).3, GPIO_OUT_4_(Level_shifted).3, U1.pin8, DS18B20_OUT2.3
  N46: GPIO_OUT_2_(Level_shifted).2, U1.pin10
  N47: GPIO_OUT_3_(Level_shifted).2, U1.pin11
  N48: GPIO_OUT_4_(Level_shifted).2, U1.pin12
  N49: USB_socket.d-, U2.pin2, U3.pin2
  N50: USB_socket.d+, U2.pin3, U3.pin3
  N51: Doser_GPIO_Out_(DB9).pin2, limit_resistors.Pin_1
  N52: Doser_GPIO_Out_(DB9).pin3, R10.Pin_1
  N53: Doser_GPIO_Out_(DB9).pin4, R11.Pin_1
  N54: Doser_GPIO_Out_(DB9).pin5, R12.Pin_1

notes:
  +12V IN
  +5V IN
  GND
  +5V
  OUT1
  OUT2
  ...
  1k Ohm pull-ups (unnecessary)
  SPI0
