# Fritzing sketch PowerUnit (saved by Fritzing 0.9.10b)
breadboards: 1

parts:
  240V_AC_Input = Power plug
  AC_Rocker_Switch = Toggle Switch [package=THT]
  AC_Sockets = Power plug
  Relay_(s) = CAR RELAY [part_number=NVF4-2 package=THT]
  10A_Fuse = FUSE [package=fuse_5mm]
  12V = 4 x AAA Battery Mount
  AC/DC_conv1 = Screw terminal - 2 pins [package=THT]
  Optocoupler = Sharp PC817 [package=THT]
  12V_+_5V_MOLEX_Adapter2 = Screw terminal - 2 pins [package=THT]
  12V_+_5V_MOLEX_Adapter = Screw terminal - 2 pins [package=THT]
  R1 = Resistor [tolerance=±5% resistance=1000 package="2512 [SMD]"]
  Q1 = TRANSISTOR_NPN [package=to-92]
  D1 = Diode [package=diode-1n4001]
  R2 = Resistor [tolerance=±5% resistance=510 package="2512 [SMD]"]
  Shorter_Header = JST-B3P-VH [part_number=JST-B3P-VH package=THT]
  optional_Short_on_VCC_(disconnected_for_isolation) = Header 2 [package=molex-1x2_lock]
  LED1 = LED - 5mm [color="Green (565nm)" current=0.030 package="5 mm [THT]"]
  Status_LEDs = LED - 5mm [color="Green (565nm)" current=0.030 package="5 mm [THT]"]
  Relay_Input_Header = Header 10 [package=1x10-2mm-smd]
  Relay_Input_HAT = Header 10 [package=1x10-2mm-smd]
  DB9_input = Header 10 [package=1x10-2mm-smd]
  IC1 = ULN2803A [package=THT]
  R3 = Resistor [tolerance=±5% power=0.25 resistance=220 package=THT]
  R4 = Resistor [tolerance=±5% power=0.25 resistance=220 package=THT]
  R5 = Resistor [tolerance=±5% power=0.25 resistance=220 package=THT]
  R6 = Resistor [tolerance=±5% power=0.25 resistance=220 package=THT]
  R7 = Resistor [tolerance=±5% power=0.25 resistance=220 package=THT]
  R8 = Resistor [tolerance=±5% power=0.25 resistance=220 package=THT]
  R9 = Resistor [tolerance=±5% power=0.25 resistance=220 package=THT]
  R10 = Resistor [tolerance=±5% power=0.25 resistance=220 package=THT]
  LED3 = LED - 5mm [color="Green (565nm)" current=0.030 package="5 mm [THT]"]
  LED4 = LED - 5mm [color="Green (565nm)" current=0.030 package="5 mm [THT]"]
  LED5 = LED - 5mm [color="Green (565nm)" current=0.030 package="5 mm [THT]"]
  LED6 = LED - 5mm [color="Green (565nm)" current=0.030 package="5 mm [THT]"]
  LED7 = LED - 5mm [color="Green (565nm)" current=0.030 package="5 mm [THT]"]
  LED9 = LED - 5mm [color="Green (565nm)" current=0.030 package="5 mm [THT]"]
  LED10 = LED - 5mm [color="Green (565nm)" current=0.030 package="5 mm [THT]"]

nets:
  N1: 240V_AC_Input.GND, 10A_Fuse.1
  N2: 240V_AC_Input.VCC, AC_Rocker_Switch.COM
  N3: AC_Rocker_Switch.L2, Relay_(s).87A, AC/DC_conv1.pin1
  N4: AC_Sockets.GND, 10A_Fuse.2, AC/DC_conv1.pin2
  N5: AC_Sockets.VCC, Relay_(s).30
  N6: Relay_(s).85, Optocoupler.Pin_4, 12V_+_5V_MOLEX_Adapter2.pin1, D1.C, Shorter_Header.pin2
  N7: Relay_(s).86, Q1.C, D1.A
  N8: 12V.-, 12V_+_5V_MOLEX_Adapter.pin2
  N9: 12V.+, 12V_+_5V_MOLEX_Adapter.pin1
  N10: Optocoupler.Pin_1, R1.Pin_1
  N11: Optocoupler.Pin_2, LED1.anode
  N12: Optocoupler.Pin_3, R2.Pin_1
  N13: 12V_+_5V_MOLEX_Adapter2.pin2, Q1.E, Shorter_Header.pin3, Relay_Input_Header.10
  N14: R1.Pin_0, Shorter_Header.pin1, Relay_Input_Header.1
  N15: Q1.B, R2.Pin_0
  N16: optional_Short_on_VCC_(disconnected_for_isolation).1, optional_Short_on_VCC_(disconnected_for_isolation).2
  N17: LED1.cathode, Relay_Input_Header.2
  N18: Status_LEDs.cathode, R3.Pin_0
  N19: Status_LEDs.anode, Relay_Input_HAT.1, DB9_input.1, IC1.COM_-_Common, LED3.anode, LED4.anode, LED5.anode, LED6.anode, LED7.anode, LED9.anode, LED10.anode
  N20: Relay_Input_HAT.2, DB9_input.2, IC1.In_1
  N21: Relay_Input_HAT.3, DB9_input.3, IC1.In_2
  N22: Relay_Input_HAT.4, DB9_input.4, IC1.In_3
  N23: Relay_Input_HAT.5, DB9_input.5, IC1.In_4
  N24: Relay_Input_HAT.6, DB9_input.6, IC1.In_5
  N25: Relay_Input_HAT.7, DB9_input.7, IC1.In_6
  N26: Relay_Input_HAT.8, DB9_input.8, IC1.In_7
  N27: Relay_Input_HAT.9, DB9_input.9, IC1.In_8
  N28: DB9_input.10, IC1.0V
  N29: IC1.Out_8, R10.Pin_1
  N30: IC1.Out_7, R9.Pin_1
  N31: IC1.Out_6, R8.Pin_1
  N32: IC1.Out_5, R7.Pin_1
  N33: IC1.Out_4, R6.Pin_1
  N34: IC1.Out_3, R5.Pin_1
  N35: IC1.Out_2, R4.Pin_1
  N36: IC1.Out_1, R3.Pin_1
  N37: R4.Pin_0, LED3.cathode
  N38: R5.Pin_0, LED4.cathode
  N39: R6.Pin_0, LED5.cathode
  N40: R7.Pin_0, LED6.cathode
  N41: R8.Pin_0, LED7.cathode
  N42: R9.Pin_0, LED9.cathode
  N43: R10.Pin_0, LED10.cathode

notes:
  GND
  VCC Relay
  VCC
  In 1
  In 2
  ...
  - AC Sockets are connected to Normally Closed
  - Relay is active (Opened) when Input is low
  - AC Status LED triggeres when Input is high
  +12V OUT
  +5V IN
